# Fritzing sketch arduino_bjt_driver (saved by Fritzing 0.9.9b)
breadboards: 1

parts:
  Q1 = NPN-Transistor [package="TO92 [THT]"]
  U1 = Arduino Uno (Rev3)
  R2 = Resistor [tolerance=±5% power=0.25 resistance=330 package=THT]
  LED1 = LED - 5mm [color="Red (633nm)" current=0.030 package="5 mm [THT]"]
  R1 = Resistor [tolerance=±5% power=0.25 resistance=2.7k package=THT]

nets:
  GND: Q1.E, U1.GND
  N1: Q1.B, R1.Pin_1
  N2: Q1.C, LED1.cathode
  N3: U1.D6_PWM, R1.Pin_0
  N4: U1.5V, R2.Pin_0
  N5: R2.Pin_1, LED1.anode
