# Fritzing sketch bjt_motor_driver (saved by Fritzing 0.9.9b)
breadboards: 1

parts:
  Componente1 = Arduino Uno (Rev3)
  Q1 = NPN-Transistor [part_number=2N2222 package="TO92 [THT]"]
  R1 = Resistor [tolerance=±5% power=0.25 resistance=330 package=THT]
  D1 = Rectifier Diode [part_number=1N4004 package="Melf DO-213 AB [SMD]"]
  M1 = DC Motor

nets:
  N1: Componente1.D9_PWM, R1.Pin_0
  GND: Componente1.GND, Q1.E
  N2: Componente1.5V, D1.cathode, M1.pin_1
  N3: Q1.B, R1.Pin_1
  N4: Q1.C, D1.anode, M1.pin_2
